# Fritzing sketch led_matrix_controller_sketch (saved by Fritzing 0.9.10b)
breadboards: 1

parts:
  Part1 = Arduino Uno (Rev3)  # not connected
  Part2 = Adafruit Proto Shield R3 [part_number="Adafruit #2077"]
  Part3 = Adafruit 8x16 LED Matrix FeatherWing - Pure Green [part_number="Adafruit #3151"]
  U1 = 74AHCT125 [part_number=SN74AHCT125 package=dil14]  # not connected
  Mod1 = Amica NodeMCU DEVKIT 1.0
  LED1 = LED - 5mm [color="Red (633nm)" current=0.030 package="5 mm [THT]"]
  R1 = Resistor [tolerance=±5% power=0.25 resistance=470 package=THT]
  R2 = Resistor [tolerance=±5% power=0.25 resistance=10000 package=THT]
  R3 = Resistor [tolerance=±5% power=0.25 resistance=10000 package=THT]
  S1 = Pushbutton [package="[THT]"]
  S2 = Pushbutton [package="[THT]"]

nets:
  N1: Part2.GND, Mod1.pin2, Mod1.pin_9, Mod1.pin_25, Mod1.pin_29, LED1.cathode, R2.Pin_0, R3.Pin_0
  N2: Part2.D0, Mod1.pin3
  N3: Part2.+5V, Part3.SDA
  N4: Part2.N$241, Part3.G
  N5: Mod1.pin1, Mod1.pin_10, Mod1.pin_26, S1.Pin_3, S1.Pin_4, S2.Pin_3, S2.Pin_4
  N6: Mod1.pin6, R2.Pin_1, S2.Pin_1, S2.Pin_2
  N7: Mod1.pin7, R3.Pin_1, S1.Pin_1, S1.Pin_2
  N8: Mod1.pin_14, R1.Pin_1
  N9: LED1.anode, R1.Pin_0

notes:
  RGB Led Matrix 32x16
  Adafruit RGB Matrix Shield
  Flat cable for RGB Matrix

custom parts:
  Adafruit Proto Shield R3: This prototyping shield is the best out there (well, we think so, at least), and now is even better with Version R3 - updated for the most compatibility with just about all the Arduinos! It works with UNO, Mega, Leonardo, NG, Diecimila, Duemilanove, and compatible Arduinos. Yun's and Arduino Ethernets have a chunky Ethernet jack that gets in the way of stacking, you can use the stacking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
  Adafruit 8x16 LED Matrix FeatherWing - Pure Green: You will chirp with delight when you see how easy it is to make your very own 8x16 LED matrix display for any Feather. This kit combines two of our adorable miniature LED matrices with a FeatherWing driver board. At 0.8" square, these little 8x8 matrices have got everything a big LED matrix has, but bite sized! Double them up for 128 total bright red LEDs. This is the Green Adafruit 0.8" 8x16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
  74AHCT125: Quad Level-Shifter (3V to 5V) Quadruple Bus Buffer Gates With 3-State Outputs
